// Logisim project CPU.circ as structural Verilog
module CUPU_II (
  input  [31:0] data_in,
  input  in_2,
  input  in_3,
  output [31:0] data_out,
  output [31:0] address
);

  wire control_1_is_alu_op, control_1_is_imm, control_1_read, control_1_reg_store, or_1_out, or_2_out;
  wire [2:0] control_1_data_bytes, control_1_s1, control_1_s2, control_1_t;
  wire [4:0] control_1_alu_op;
  wire [7:0] undriven, undriven_2, undriven_3, undriven_4;
  wire [23:0] bit_extender_1_out;
  wire [31:0] alu_1_res, control_1_data_out, multiplexer_1_out, multiplexer_2_out, regs_1_data_out1,
       regs_1_data_out2;

  control control_1 (
    .imm_data({undriven_4, undriven_3, undriven_2, undriven}), .data_in(multiplexer_1_out), .t(control_1_t),
    .s1(control_1_s1), .s2(control_1_s2), .data_bytes(control_1_data_bytes), .read(control_1_read),
    .address(address), .data_out(control_1_data_out), .reg_store(control_1_reg_store),
    .is_imm(control_1_is_imm), .is_ALU_op(control_1_is_alu_op), .ALU_op(control_1_alu_op));  // open: write
  Multiplexer #(.width(32)) multiplexer_1 (
    .in0(regs_1_data_out1), .in1(alu_1_res), .out(multiplexer_1_out), .sel(control_1_is_alu_op));
  regs regs_1 (
    .load(control_1_reg_store), .target(control_1_t), .source1(control_1_s1), .source2(control_1_s2),
    .data_in(alu_1_res), .data_out1(regs_1_data_out1), .data_out2(regs_1_data_out2));
  Bit_Extender #(.in_width(32), .out_width(24), .\type ("zero")) bit_extender_1 (
    .in(address), .out(bit_extender_1_out));
  ALU alu_1 (.a(regs_1_data_out1), .b(multiplexer_2_out), .op(control_1_alu_op), .res(alu_1_res));
  Multiplexer #(.width(32)) multiplexer_2 (
    .in0(regs_1_data_out2), .in1(control_1_data_out), .out(multiplexer_2_out), .sel(control_1_is_imm));
  or or_1 (or_1_out, control_1_data_bytes[0], control_1_data_bytes[1], control_1_data_bytes[2]);
  or or_2 (or_2_out, control_1_data_bytes[1], control_1_data_bytes[2]);
  // Probe on {undriven_4, undriven_3, undriven_2, undriven}
  // RAM #(.addrWidth(24), .clearpin("true"), .enables("line"), .line("quad"), .misaligned("true"), .\type ("nonvolatile")) ram_1: pin names not known; wires that end beside it: in_3, bit_extender_1_out, or_1_out, or_2_out, control_1_data_bytes[2], control_1_data_bytes[2]
endmodule

module regs (
  input  load,
  input  [2:0] target,
  input  [2:0] source1,
  input  [2:0] source2,
  input  [31:0] data_in,
  output [31:0] data_out1,
  output [31:0] data_out2
);

  wire decoder_1_out1, decoder_1_out2, decoder_1_out3, decoder_1_out4, decoder_1_out5, decoder_1_out6,
       decoder_1_out7;
  wire [31:0] register_1_q, register_2_q, register_3_q, register_4_q, register_5_q, register_6_q,
       register_7_q;

  Decoder #(.select(3)) decoder_1 (
    .out1(decoder_1_out1), .out2(decoder_1_out2), .out3(decoder_1_out3), .out4(decoder_1_out4),
    .out5(decoder_1_out5), .out6(decoder_1_out6), .out7(decoder_1_out7), .sel(target), .en(load));  // open: out0
  Register #(.trigger("falling"), .width(32)) register_1 (
    .D(data_in), .Q(register_1_q), .clk(decoder_1_out1));  // open: en, clr
  Register #(.trigger("falling"), .width(32)) register_2 (
    .D(data_in), .Q(register_2_q), .clk(decoder_1_out2));  // open: en, clr
  Register #(.trigger("falling"), .width(32)) register_3 (
    .D(data_in), .Q(register_3_q), .clk(decoder_1_out3));  // open: en, clr
  Register #(.trigger("falling"), .width(32)) register_4 (
    .D(data_in), .Q(register_4_q), .clk(decoder_1_out4));  // open: en, clr
  Register #(.trigger("falling"), .width(32)) register_5 (
    .D(data_in), .Q(register_5_q), .clk(decoder_1_out5));  // open: en, clr
  Register #(.trigger("falling"), .width(32)) register_6 (
    .D(data_in), .Q(register_6_q), .clk(decoder_1_out6));  // open: en, clr
  Register #(.trigger("falling"), .width(32)) register_7 (
    .D(data_in), .Q(register_7_q), .clk(decoder_1_out7));  // open: en, clr
  Multiplexer #(.select(3), .width(32)) multiplexer_1 (
    .in0({32{1'b0}}), .in1(register_1_q), .in2(register_2_q), .in3(register_3_q), .in4(register_4_q),
    .in5(register_5_q), .in6(register_6_q), .in7(register_7_q), .out(data_out1), .sel(source1));
  Multiplexer #(.select(3), .width(32)) multiplexer_2 (
    .in0({32{1'b0}}), .in1(register_1_q), .in2(register_2_q), .in3(register_3_q), .in4(register_4_q),
    .in5(register_5_q), .in6(register_6_q), .in7(register_7_q), .out(data_out2), .sel(source2));
endmodule

module decode (
  input  [2:0] in_1,
  input  [31:0] in_2,
  output [31:0] out_3
);

  wire [31:0] bit_extender_1_out, bit_extender_2_out, bit_extender_3_out, bit_extender_4_out;

  assign bit_extender_1_out = {{24{in_2[7]}}, in_2[7:0]};  // Bit_Extender bit_extender_1
  assign bit_extender_2_out = {{16{in_2[15]}}, in_2[15:0]};  // Bit_Extender bit_extender_2
  assign bit_extender_3_out = {{24{1'b0}}, in_2[7:0]};  // Bit_Extender bit_extender_3
  assign bit_extender_4_out = {{16{1'b0}}, in_2[15:0]};  // Bit_Extender bit_extender_4
  Multiplexer #(.select(3), .width(32)) multiplexer_1 (
    .in0(bit_extender_1_out), .in1(bit_extender_2_out), .in2(in_2), .in4(bit_extender_3_out),
    .in5(bit_extender_4_out), .out(out_3), .sel(in_1));  // open: in3, in6, in7
endmodule

module ALU (
  input  [31:0] a,
  input  [31:0] b,
  input  [4:0] op,
  output [31:0] res
);

  wire adder_1_cout, adder_2_cout, subtractor_1_bout, subtractor_2_bout;
  wire [4:0] bit_extender_1_out, bit_extender_2_out, bit_extender_3_out;
  wire [31:0] adder_1_out, adder_2_out, and_1_out, bit_extender_4_out, bit_extender_5_out,
       bit_extender_6_out, bit_extender_7_out, divider_1_out, divider_1_rem, divider_2_out, divider_2_rem,
       fpadder_1_out, fpdivider_1_out, fpmultiplier_1_out, fpsubtractor_1_out, fptoint_1_p2, inttofp_1_p2,
       multiplier_1_cout, multiplier_1_out, multiplier_2_cout, not_1_out, or_1_out, shifter_1_out,
       shifter_2_out, subtractor_1_out, subtractor_2_out, xor_1_out;

  Adder #(.width(32)) adder_1 (.a(a), .b(b), .out(adder_1_out), .cout(adder_1_cout));  // open: cin
  Subtractor #(.width(32)) subtractor_1 (.a(a), .b(b), .out(subtractor_1_out), .bout(subtractor_1_bout));  // open: bin
  Multiplier #(.mode("twosComplement"), .width(32)) multiplier_1 (
    .a(a), .b(b), .out(multiplier_1_out), .cout(multiplier_1_cout));  // open: cin
  Multiplier #(.width(32)) multiplier_2 (.a(a), .b(b), .cout(multiplier_2_cout));  // open: out, cin
  Divider #(.mode("twosComplement"), .width(32)) divider_1 (
    .a(a), .b(b), .out(divider_1_out), .rem(divider_1_rem));  // open: upper
  Divider #(.width(32)) divider_2 (.a(a), .b(b), .out(divider_2_out), .rem(divider_2_rem));  // open: upper
  Adder #(.width(32)) adder_2 (.a(a), .b(32'h1), .out(adder_2_out), .cout(adder_2_cout));  // open: cin
  Subtractor #(.width(32)) subtractor_2 (
    .a(a), .b(32'h1), .out(subtractor_2_out), .bout(subtractor_2_bout));  // open: bin
  FPAdder fpadder_1 (.a(a), .b(b), .out(fpadder_1_out));
  FPSubtractor fpsubtractor_1 (.a(a), .b(b), .out(fpsubtractor_1_out));
  FPMultiplier fpmultiplier_1 (.a(a), .b(b), .out(fpmultiplier_1_out));
  FPDivider fpdivider_1 (.a(a), .b(b), .out(fpdivider_1_out));
  // IntToFP #(.width(32)) inttofp_1: pin names not known; wires that end beside it: a, inttofp_1_p2
  // FPToInt #(.width(32)) fptoint_1: pin names not known; wires that end beside it: a, fptoint_1_p2
  assign or_1_out = a | b;  // OR_Gate or_1, 32 bits wide
  assign and_1_out = a & b;  // AND_Gate and_1, 32 bits wide
  assign xor_1_out = a ^ b;  // XOR_Gate xor_1, 32 bits wide
  assign not_1_out = ~a;  // NOT_Gate not_1, 32 bits wide
  Bit_Extender #(.in_width(32), .out_width(5), .\type ("zero")) bit_extender_1 (.in(b), .out(bit_extender_1_out));
  Bit_Extender #(.in_width(32), .out_width(5), .\type ("zero")) bit_extender_2 (.in(b), .out(bit_extender_2_out));
  Bit_Extender #(.in_width(32), .out_width(5), .\type ("zero")) bit_extender_3 (.in(b), .out(bit_extender_3_out));
  assign bit_extender_4_out = {{31{1'b0}}, adder_1_cout};  // Bit_Extender bit_extender_4
  assign bit_extender_5_out = {{31{1'b0}}, subtractor_1_bout};  // Bit_Extender bit_extender_5
  assign bit_extender_6_out = {{31{1'b0}}, adder_2_cout};  // Bit_Extender bit_extender_6
  assign bit_extender_7_out = {{31{1'b0}}, subtractor_2_bout};  // Bit_Extender bit_extender_7
  Shifter #(.width(32)) shifter_1 (.in(a), .\dist (bit_extender_1_out), .out(shifter_1_out));
  Shifter #(.shift("lr"), .width(32)) shifter_2 (.in(a), .\dist (bit_extender_2_out), .out(shifter_2_out));
  Shifter #(.shift("ar"), .width(32)) shifter_3 (.in(a), .\dist (bit_extender_3_out));  // open: out
  Multiplexer #(.select(5), .width(32)) multiplexer_1 (
    .in0(adder_1_out), .in1(bit_extender_4_out), .in2(subtractor_1_out), .in3(bit_extender_5_out),
    .in4(multiplier_1_out), .in5(multiplier_1_cout), .in6(multiplier_2_cout), .in7(divider_1_out),
    .in8(divider_2_out), .in9(divider_1_rem), .in10(divider_2_rem), .in11(adder_2_out),
    .in12(bit_extender_6_out), .in13(subtractor_2_out), .in14(bit_extender_7_out), .in15(fpadder_1_out),
    .in16(fpsubtractor_1_out), .in17(fpmultiplier_1_out), .in18(fpdivider_1_out), .in19(inttofp_1_p2),
    .in20(fptoint_1_p2), .in21(a), .in22(or_1_out), .in23(and_1_out), .in24(xor_1_out), .in25(not_1_out),
    .in26(shifter_1_out), .in27(shifter_2_out), .out(res), .sel(op));  // open: in28, in29, in30, in31
endmodule

module control (
  input  [31:0] imm_data,
  input  [31:0] data_in,
  output [2:0] t,
  output [2:0] s1,
  output [2:0] s2,
  output [2:0] data_bytes,
  output write,
  output read,
  output [31:0] address,
  output [31:0] data_out,
  output reg_store,
  output is_imm,
  output is_ALU_op,
  output [4:0] ALU_op
);

  wire and_1_out, and_2_out, and_3_out, and_4_out, and_5_out, and_8_out, and_9_out, and_10_out, clock_1_out,
       decoder_1_out0, decoder_1_out1, decoder_1_out2, decoder_2_out0, decoder_2_out1, decoder_2_out2,
       decoder_2_out3, decoder_3_out0, decoder_3_out1, decoder_3_out2, decoder_3_out3, decoder_3_out4,
       decoder_3_out5, decoder_3_out6, decoder_3_out7, not_1_out, or_1_out, or_2_out, or_3_out;
  wire [2:0] counter_1_q, multiplexer_1_out, multiplexer_2_out;
  wire [15:0] bit_extender_1_out;
  wire [15:15] register_1_q;
  wire [31:0] adder_1_out, pc_1_address, register_2_q;

  Counter #(.max('h7), .trigger("falling"), .width(3)) counter_1 (
    .Q(counter_1_q), .clk(clock_1_out), .clr(and_1_out));  // open: load, D, count, carry, up
  Clock clock_1 (.out(clock_1_out));
  and and_1 (and_1_out, ~clock_1_out, and_2_out);  // AND_Gate
  decode decode_1 (.in_1(multiplexer_1_out), .in_2(imm_data), .out_3(data_out));
  Decoder #(.select(3)) decoder_1 (
    .out0(decoder_1_out0), .out1(decoder_1_out1), .out2(decoder_1_out2), .sel(counter_1_q), .en(clock_1_out));  // open: out3, out4, out5, out6, out7
  and and_2 (and_2_out, decoder_1_out2, is_ALU_op);
  Adder #(.width(32)) adder_1 (.a(data_out), .b(data_in), .out(adder_1_out));  // open: cin, cout
  Bit_Extender #(.in_width(32), .\type ("zero")) bit_extender_1 (.in(imm_data), .out(bit_extender_1_out));
  Register #(.width(16)) register_1 (
    .D(bit_extender_1_out), .Q({register_1_q[15], is_imm, ALU_op, t, s1, s2}), .clk(decoder_1_out0));  // open: en, clr
  Decoder #(.select(2)) decoder_2 (
    .out0(decoder_2_out0), .out1(decoder_2_out1), .out2(decoder_2_out2), .out3(decoder_2_out3),
    .sel(ALU_op[1:0]), .en(register_1_q[15]));
  Decoder #(.select(3)) decoder_3 (
    .out0(decoder_3_out0), .out1(decoder_3_out1), .out2(decoder_3_out2), .out3(decoder_3_out3),
    .out4(decoder_3_out4), .out5(decoder_3_out5), .out6(decoder_3_out6), .out7(decoder_3_out7),
    .sel(ALU_op[4:2]), .en(register_1_q[15]));
  and and_3 (and_3_out, is_imm, decoder_1_out2);
  not not_1 (not_1_out, register_1_q[15]);
  buf or_1 (or_1_out, not_1_out);  // OR_Gate
  and and_4 (and_4_out, and_3_out, or_1_out);
  not not_2 (is_ALU_op, register_1_q[15]);
  or or_2 (or_2_out, is_ALU_op, decoder_3_out1, and_5_out, decoder_3_out5);
  or or_3 (or_3_out, decoder_2_out0, decoder_2_out3);
  and and_5 (and_5_out, decoder_3_out3, or_3_out);
  and and_6 (reg_store, or_2_out, decoder_1_out1);
  // AND_Gate and_7 is placed but not wired
  and and_8 (and_8_out, decoder_2_out0, decoder_3_out1, decoder_1_out2);
  and and_9 (and_9_out, decoder_2_out1, decoder_3_out0);
  PC pc_1 (
    .imm_data_type(multiplexer_1_out), .skip_imm(and_4_out), .jump(and_8_out), .clk(decoder_1_out0),
    .data(adder_1_out), .address(pc_1_address));  // open: jump_relative
  Multiplexer #(.width(3)) multiplexer_1 (.in0(s2), .in1(t), .out(multiplexer_1_out), .sel(and_9_out));
  buf and_10 (and_10_out, decoder_3_out0);  // AND_Gate
  Register #(.width(32)) register_2 (.D(adder_1_out), .Q(register_2_q));  // open: en, clk, clr
  Multiplexer #(.select(3), .width(3)) multiplexer_2 (
    .in0(3'b001), .in1(3'b010), .in2(3'b100), .in4(3'b001), .in5(3'b010), .out(multiplexer_2_out),
    .sel(multiplexer_1_out));  // open: in3, in6, in7
  Multiplexer #(.width(32)) multiplexer_3 (.in0(pc_1_address), .in1(register_2_q), .out(address), .sel(and_10_out));
  Multiplexer #(.width(3)) multiplexer_4 (
    .in0(multiplexer_2_out), .in1(3'b010), .out(data_bytes), .sel(decoder_1_out0));
  or or_4 (read, reg_store, decoder_1_out0);
endmodule

module PC (
  input  [2:0] imm_data_type,
  input  skip_imm,
  input  jump,
  input  jump_relative,
  input  clk,
  input  [31:0] data,
  output [31:0] address
);

  wire or_1_out;
  wire [31:0] adder_1_out, adder_2_out, multiplexer_1_out, multiplexer_2_out, multiplexer_3_out,
       multiplexer_4_out;

  Multiplexer #(.width(32)) multiplexer_1 (
    .in0(32'h2), .in1(multiplexer_2_out), .out(multiplexer_1_out), .sel(skip_imm));
  Multiplexer #(.select(3), .width(32)) multiplexer_2 (
    .in0(32'h1), .in1(32'h2), .in2(32'h4), .in4(32'h1), .in5(32'h2), .out(multiplexer_2_out),
    .sel(imm_data_type));  // open: in3, in6, in7
  Adder #(.width(32)) adder_1 (.a(multiplexer_1_out), .b(address), .out(adder_1_out));  // open: cin, cout
  Multiplexer #(.width(32)) multiplexer_3 (.in0(adder_1_out), .in1(data), .out(multiplexer_3_out), .sel(jump));
  Adder #(.width(32)) adder_2 (.a(address), .b(data), .out(adder_2_out));  // open: cin, cout
  Multiplexer #(.width(32)) multiplexer_4 (
    .in0(multiplexer_3_out), .in1(adder_2_out), .out(multiplexer_4_out), .sel(jump_relative));
  Register #(.trigger("falling"), .width(32)) register_1 (
    .D(multiplexer_4_out), .Q(address), .clk(or_1_out));  // open: en, clr
  or or_1 (or_1_out, skip_imm, jump, jump_relative, clk);
endmodule

module delay (
  input  in_1,
  output out_2
);

  wire buffer_1_out, buffer_2_out, buffer_3_out, buffer_4_out, buffer_5_out, buffer_6_out, buffer_7_out,
       buffer_8_out, buffer_9_out, buffer_10_out, buffer_11_out, buffer_12_out, buffer_13_out, buffer_14_out,
       buffer_15_out, buffer_16_out, buffer_17_out, buffer_18_out, buffer_19_out, buffer_20_out,
       buffer_21_out, buffer_22_out;

  buf buffer_1 (buffer_1_out, buffer_4_out);
  buf buffer_2 (buffer_2_out, buffer_1_out);
  buf buffer_3 (buffer_3_out, buffer_2_out);
  buf buffer_4 (buffer_4_out, in_1);
  buf buffer_5 (buffer_5_out, buffer_3_out);
  buf buffer_6 (buffer_6_out, buffer_5_out);
  buf buffer_7 (buffer_7_out, buffer_6_out);
  buf buffer_8 (buffer_8_out, buffer_7_out);
  buf buffer_9 (buffer_9_out, buffer_8_out);
  buf buffer_10 (buffer_10_out, buffer_9_out);
  buf buffer_11 (buffer_11_out, buffer_10_out);
  buf buffer_12 (buffer_12_out, buffer_11_out);
  buf buffer_13 (buffer_13_out, buffer_12_out);
  buf buffer_14 (buffer_14_out, buffer_13_out);
  buf buffer_15 (buffer_15_out, buffer_14_out);
  buf buffer_16 (buffer_16_out, buffer_15_out);
  buf buffer_17 (buffer_17_out, buffer_16_out);
  buf buffer_18 (buffer_18_out, buffer_17_out);
  buf buffer_19 (buffer_19_out, buffer_18_out);
  buf buffer_20 (buffer_20_out, buffer_19_out);
  buf buffer_21 (buffer_21_out, buffer_20_out);
  buf buffer_22 (buffer_22_out, buffer_21_out);
  buf buffer_23 (out_2, buffer_22_out);
endmodule

module bin_to_hex_inst_converter (
);

  wire [3:0] dipswitch_1_p1, dipswitch_2_p3, dipswitch_4_p1, dipswitch_5_p2;

  // DipSwitch #(.number(3)) dipswitch_1: pin names not known; wires that end beside it: dipswitch_1_p1[0], dipswitch_1_p1[1]
  // DipSwitch #(.number(3)) dipswitch_2: pin names not known; wires that end beside it: dipswitch_1_p1[2], dipswitch_1_p1[3], dipswitch_2_p3[0]
  // DipSwitch #(.number(3)) dipswitch_3: pin names not known; wires that end beside it: dipswitch_2_p3[1], dipswitch_2_p3[2], dipswitch_2_p3[3]
  // DipSwitch #(.number(2)) dipswitch_4: pin names not known; wires that end beside it: dipswitch_4_p1[0], dipswitch_4_p1[1], dipswitch_4_p1[2]
  // DipSwitch #(.number(3)) dipswitch_5: pin names not known; wires that end beside it: dipswitch_4_p1[3], dipswitch_5_p2[0]
  // DipSwitch #(.number(2)) dipswitch_6: pin names not known; wires that end beside it: dipswitch_5_p2[1], dipswitch_5_p2[2], dipswitch_5_p2[3]
  Hex_Digit_Display hex_digit_display_1 (.value(dipswitch_2_p3));  // open: dp
  Hex_Digit_Display hex_digit_display_2 (.value(dipswitch_1_p1));  // open: dp
  Hex_Digit_Display hex_digit_display_3 (.value(dipswitch_5_p2));  // open: dp
  Hex_Digit_Display hex_digit_display_4 (.value(dipswitch_4_p1));  // open: dp
endmodule
