// Logisim project CUPU_II.circ as structural Verilog
module cpu (
  input  [31:0] in_1,
  output [31:0] out_2,
  output [31:0] out_3,
  output out_4,
  output out_5
);

  wire clock_1_out, decode_1_alu, decode_1_comp, decode_1_is_imm, decode_1_jmp, decode_1_lui,
       decode_1_reg_store, decode_1_rel_jmp, machine_cycle_1_out_2, machine_cycle_1_out_5, or_1_out;
  wire [4:0] decode_1_a, decode_1_b, decode_1_t;
  wire [10:0] decode_1_func11;
  wire [31:0] adder_1_out, alu_1_out_5, decode_1_imm, multiplexer_1_out, multiplexer_2_out,
       multiplexer_3_out, pc_1_out_val, register_1_q, regs_1_out_2, regs_1_out_3;

  Clock clock_1 (.out(clock_1_out));
  Register #(.width(32)) register_1 (.D(in_1), .Q(register_1_q), .clk(machine_cycle_1_out_2));  // open: en, clr
  decode decode_1 (
    .in_1(register_1_q), .func11(decode_1_func11), .b(decode_1_b), .a(decode_1_a), .t(decode_1_t),
    .alu(decode_1_alu), .comp(decode_1_comp), .reg_store(decode_1_reg_store), .jmp(decode_1_jmp),
    .rel_jmp(decode_1_rel_jmp), .imm(decode_1_imm), .is_imm(decode_1_is_imm), .lui(decode_1_lui));  // open: mem, load, store, hlt, cond
  machine_cycle machine_cycle_1 (
    .in_1(clock_1_out), .out_2(machine_cycle_1_out_2), .out_5(machine_cycle_1_out_5));  // open: out_3, out_4
  alu alu_1 (
    .a(regs_1_out_2), .b(multiplexer_1_out), .func(decode_1_func11), .enable(decode_1_alu),
    .out_5(alu_1_out_5));
  Multiplexer #(.width(32)) multiplexer_1 (
    .in0(regs_1_out_3), .in1(decode_1_imm), .out(multiplexer_1_out), .sel(decode_1_is_imm));
  pc pc_1 (
    .jump_relative(decode_1_rel_jmp), .jump(decode_1_jmp), .tick(machine_cycle_1_out_5),
    .out_val(pc_1_out_val));  // open: in_val
  or or_1 (or_1_out, decode_1_rel_jmp, decode_1_jmp);
  Multiplexer #(.width(32)) multiplexer_2 (
    .in0(alu_1_out_5), .in1(decode_1_imm), .out(multiplexer_2_out), .sel(decode_1_lui));
  Adder #(.width(32)) adder_1 (.a(pc_1_out_val), .b(32'h4), .out(adder_1_out));  // open: cin, cout
  Multiplexer #(.width(32)) multiplexer_3 (
    .in0(multiplexer_2_out), .in1(adder_1_out), .out(multiplexer_3_out), .sel(or_1_out));
  regs regs_1 (
    .enable(decode_1_reg_store), .out_2(regs_1_out_2), .out_3(regs_1_out_3), .t(decode_1_t), .a(decode_1_a),
    .b(decode_1_b), .\input (multiplexer_3_out), .store(machine_cycle_1_out_5));
  comp comp_1 (
    .a(regs_1_out_2), .b(regs_1_out_3), .func11(decode_1_func11), .enable(decode_1_comp),
    .save_cond(machine_cycle_1_out_5));  // open: out_6
endmodule

module pc (
  input  [31:0] in_val,
  input  jump_relative,
  input  jump,
  input  tick,
  output [31:0] out_val
);

  wire [31:0] adder_1_out, multiplexer_1_out, multiplexer_2_out;

  Multiplexer #(.width(32)) multiplexer_1 (.in0(32'h4), .in1(in_val), .out(multiplexer_1_out), .sel(jump_relative));
  Adder #(.width(32)) adder_1 (.a(multiplexer_1_out), .b(out_val), .out(adder_1_out));  // open: cin, cout
  Multiplexer #(.width(32)) multiplexer_2 (.in0(adder_1_out), .in1(in_val), .out(multiplexer_2_out), .sel(jump));
  Register #(.trigger("falling"), .width(32)) register_1 (
    .D(multiplexer_2_out), .Q(out_val), .clk(tick));  // open: en, clr
endmodule

module machine_cycle (
  input  in_1,
  output out_2,
  output out_3,
  output out_4,
  output out_5
);

  wire [1:0] counter_1_q;

  Counter #(.max('h3), .trigger("falling"), .width(2)) counter_1 (
    .Q(counter_1_q), .clk(in_1));  // open: load, D, count, carry, up, clr
  Decoder #(.select(2)) decoder_1 (
    .out0(out_2), .out1(out_3), .out2(out_4), .out3(out_5), .sel(counter_1_q), .en(in_1));
endmodule

module regs (
  input  enable,
  output [31:0] out_2,
  output [31:0] out_3,
  output [4:0] t,
  output [4:0] a,
  output [4:0] b,
  output [31:0] \input ,
  output store
);

  wire decoder_1_out1, decoder_1_out2, decoder_1_out3, decoder_1_out4, decoder_1_out5, decoder_1_out6,
       decoder_1_out7, decoder_1_out8, decoder_1_out9, decoder_1_out10, decoder_1_out11, decoder_1_out12,
       decoder_1_out13, decoder_1_out14, decoder_1_out15, decoder_1_out16, decoder_1_out17, decoder_1_out18,
       decoder_1_out19, decoder_1_out20, decoder_1_out21, decoder_1_out22, decoder_1_out23, decoder_1_out24,
       decoder_1_out25, decoder_1_out26, decoder_1_out27, decoder_1_out28, decoder_1_out29, decoder_1_out30,
       decoder_1_out31;
  wire [31:0] pull_resistor_1_node, register_1_q, register_2_q, register_3_q, register_4_q, register_5_q,
       register_6_q, register_7_q, register_8_q, register_9_q, register_10_q, register_11_q, register_12_q,
       register_13_q, register_14_q, register_15_q, register_16_q, register_17_q, register_18_q,
       register_19_q, register_20_q, register_21_q, register_22_q, register_23_q, register_24_q,
       register_25_q, register_26_q, register_27_q, register_28_q, register_29_q, register_30_q,
       register_31_q;

  Decoder #(.select(5)) decoder_1 (
    .out1(decoder_1_out1), .out2(decoder_1_out2), .out3(decoder_1_out3), .out4(decoder_1_out4),
    .out5(decoder_1_out5), .out6(decoder_1_out6), .out7(decoder_1_out7), .out8(decoder_1_out8),
    .out9(decoder_1_out9), .out10(decoder_1_out10), .out11(decoder_1_out11), .out12(decoder_1_out12),
    .out13(decoder_1_out13), .out14(decoder_1_out14), .out15(decoder_1_out15), .out16(decoder_1_out16),
    .out17(decoder_1_out17), .out18(decoder_1_out18), .out19(decoder_1_out19), .out20(decoder_1_out20),
    .out21(decoder_1_out21), .out22(decoder_1_out22), .out23(decoder_1_out23), .out24(decoder_1_out24),
    .out25(decoder_1_out25), .out26(decoder_1_out26), .out27(decoder_1_out27), .out28(decoder_1_out28),
    .out29(decoder_1_out29), .out30(decoder_1_out30), .out31(decoder_1_out31), .sel(t), .en(enable));  // open: out0
  Pull_Resistor pull_resistor_1 (.node(pull_resistor_1_node));
  Register #(.width(32)) register_1 (.D(\input ), .en(decoder_1_out1), .Q(register_1_q), .clk(store));  // open: clr
  Register #(.width(32)) register_2 (.D(\input ), .en(decoder_1_out2), .Q(register_2_q), .clk(store));  // open: clr
  Register #(.width(32)) register_3 (.D(\input ), .en(decoder_1_out3), .Q(register_3_q), .clk(store));  // open: clr
  Register #(.width(32)) register_4 (.D(\input ), .en(decoder_1_out4), .Q(register_4_q), .clk(store));  // open: clr
  Register #(.width(32)) register_5 (.D(\input ), .en(decoder_1_out5), .Q(register_5_q), .clk(store));  // open: clr
  Register #(.width(32)) register_6 (.D(\input ), .en(decoder_1_out6), .Q(register_6_q), .clk(store));  // open: clr
  Register #(.width(32)) register_7 (.D(\input ), .en(decoder_1_out7), .Q(register_7_q), .clk(store));  // open: clr
  Register #(.width(32)) register_8 (.D(\input ), .en(decoder_1_out8), .Q(register_8_q), .clk(store));  // open: clr
  Register #(.width(32)) register_9 (.D(\input ), .en(decoder_1_out9), .Q(register_9_q), .clk(store));  // open: clr
  Register #(.width(32)) register_10 (.D(\input ), .en(decoder_1_out10), .Q(register_10_q), .clk(store));  // open: clr
  Register #(.width(32)) register_11 (.D(\input ), .en(decoder_1_out11), .Q(register_11_q), .clk(store));  // open: clr
  Register #(.width(32)) register_12 (.D(\input ), .en(decoder_1_out12), .Q(register_12_q), .clk(store));  // open: clr
  Register #(.width(32)) register_13 (.D(\input ), .en(decoder_1_out13), .Q(register_13_q), .clk(store));  // open: clr
  Register #(.width(32)) register_14 (.D(\input ), .en(decoder_1_out14), .Q(register_14_q), .clk(store));  // open: clr
  Register #(.width(32)) register_15 (.D(\input ), .en(decoder_1_out15), .Q(register_15_q), .clk(store));  // open: clr
  Register #(.width(32)) register_16 (.D(\input ), .en(decoder_1_out16), .Q(register_16_q), .clk(store));  // open: clr
  Register #(.width(32)) register_17 (.D(\input ), .en(decoder_1_out17), .Q(register_17_q), .clk(store));  // open: clr
  Register #(.width(32)) register_18 (.D(\input ), .en(decoder_1_out18), .Q(register_18_q), .clk(store));  // open: clr
  Register #(.width(32)) register_19 (.D(\input ), .en(decoder_1_out19), .Q(register_19_q), .clk(store));  // open: clr
  Register #(.width(32)) register_20 (.D(\input ), .en(decoder_1_out20), .Q(register_20_q), .clk(store));  // open: clr
  Register #(.width(32)) register_21 (.D(\input ), .en(decoder_1_out21), .Q(register_21_q), .clk(store));  // open: clr
  Register #(.width(32)) register_22 (.D(\input ), .en(decoder_1_out22), .Q(register_22_q), .clk(store));  // open: clr
  Register #(.width(32)) register_23 (.D(\input ), .en(decoder_1_out23), .Q(register_23_q), .clk(store));  // open: clr
  Register #(.width(32)) register_24 (.D(\input ), .en(decoder_1_out24), .Q(register_24_q), .clk(store));  // open: clr
  Register #(.width(32)) register_25 (.D(\input ), .en(decoder_1_out25), .Q(register_25_q), .clk(store));  // open: clr
  Register #(.width(32)) register_26 (.D(\input ), .en(decoder_1_out26), .Q(register_26_q), .clk(store));  // open: clr
  Register #(.width(32)) register_27 (.D(\input ), .en(decoder_1_out27), .Q(register_27_q), .clk(store));  // open: clr
  Register #(.width(32)) register_28 (.D(\input ), .en(decoder_1_out28), .Q(register_28_q), .clk(store));  // open: clr
  Register #(.width(32)) register_29 (.D(\input ), .en(decoder_1_out29), .Q(register_29_q), .clk(store));  // open: clr
  Register #(.width(32)) register_30 (.D(\input ), .en(decoder_1_out30), .Q(register_30_q), .clk(store));  // open: clr
  Register #(.width(32)) register_31 (.D(\input ), .en(decoder_1_out31), .Q(register_31_q), .clk(store));  // open: clr
  Multiplexer #(.select(5), .width(32)) multiplexer_1 (
    .in0(pull_resistor_1_node), .in1(register_1_q), .in2(register_2_q), .in3(register_3_q),
    .in4(register_4_q), .in5(register_5_q), .in6(register_6_q), .in7(register_7_q), .in8(register_8_q),
    .in9(register_9_q), .in10(register_10_q), .in11(register_11_q), .in12(register_12_q),
    .in13(register_13_q), .in14(register_14_q), .in15(register_15_q), .in16(register_16_q),
    .in17(register_17_q), .in18(register_18_q), .in19(register_19_q), .in20(register_20_q),
    .in21(register_21_q), .in22(register_22_q), .in23(register_23_q), .in24(register_24_q),
    .in25(register_25_q), .in26(register_26_q), .in27(register_27_q), .in28(register_28_q),
    .in29(register_29_q), .in30(register_30_q), .in31(register_31_q), .out(out_2), .sel(a));
  Multiplexer #(.select(5), .width(32)) multiplexer_2 (
    .in0(pull_resistor_1_node), .in1(register_1_q), .in2(register_2_q), .in3(register_3_q),
    .in4(register_4_q), .in5(register_5_q), .in6(register_6_q), .in7(register_7_q), .in8(register_8_q),
    .in9(register_9_q), .in10(register_10_q), .in11(register_11_q), .in12(register_12_q),
    .in13(register_13_q), .in14(register_14_q), .in15(register_15_q), .in16(register_16_q),
    .in17(register_17_q), .in18(register_18_q), .in19(register_19_q), .in20(register_20_q),
    .in21(register_21_q), .in22(register_22_q), .in23(register_23_q), .in24(register_24_q),
    .in25(register_25_q), .in26(register_26_q), .in27(register_27_q), .in28(register_28_q),
    .in29(register_29_q), .in30(register_30_q), .in31(register_31_q), .out(out_3), .sel(b));
endmodule

module alu (
  input  [31:0] a,
  input  [31:0] b,
  input  [10:0] func,
  input  enable,
  output [31:0] out_5
);

  wire adder_1_cout, subtractor_1_bout;
  wire [4:0] bit_extender_1_out, bit_extender_2_out, bit_extender_3_out;
  wire [31:0] adder_1_out, and_1_out, bit_extender_4_out, bit_extender_5_out, divider_1_out, divider_1_rem,
       fpadder_1_out, fpdivider_1_out, fpmultiplier_1_out, fpsquareroot_1_p2, fpsubtractor_1_out,
       fptoint_1_p2, fptrigonometry_1_p2, fptrigonometry_1_p3, fptrigonometry_1_p4, inttofp_1_p2,
       multiplier_1_cout, multiplier_1_out, not_1_out, or_1_out, pull_resistor_1_node, pull_resistor_2_node,
       shifter_1_out, shifter_2_out, subtractor_1_out, xor_1_out;

  Bit_Extender #(.in_width(32), .out_width(5)) bit_extender_1 (.in(pull_resistor_2_node), .out(bit_extender_1_out));
  Bit_Extender #(.in_width(32), .out_width(5)) bit_extender_2 (.in(pull_resistor_2_node), .out(bit_extender_2_out));
  Pull_Resistor pull_resistor_1 (.node(pull_resistor_1_node));
  assign pull_resistor_1_node = enable ? a : 32'bz;  // Controlled_Buffer controlled_buffer_1
  Pull_Resistor pull_resistor_2 (.node(pull_resistor_2_node));
  assign pull_resistor_2_node = enable ? b : 32'bz;  // Controlled_Buffer controlled_buffer_2
  Adder #(.width(32)) adder_1 (
    .a(pull_resistor_1_node), .b(pull_resistor_2_node), .out(adder_1_out), .cout(adder_1_cout));  // open: cin
  Subtractor #(.width(32)) subtractor_1 (
    .a(pull_resistor_1_node), .b(pull_resistor_2_node), .out(subtractor_1_out), .bout(subtractor_1_bout));  // open: bin
  Multiplier #(.width(32)) multiplier_1 (
    .a(pull_resistor_1_node), .b(pull_resistor_2_node), .out(multiplier_1_out), .cout(multiplier_1_cout));  // open: cin
  Divider #(.width(32)) divider_1 (
    .a(pull_resistor_1_node), .b(pull_resistor_2_node), .out(divider_1_out), .rem(divider_1_rem));  // open: upper
  assign or_1_out = pull_resistor_1_node | pull_resistor_2_node;  // OR_Gate or_1, 32 bits wide
  assign and_1_out = pull_resistor_1_node & pull_resistor_2_node;  // AND_Gate and_1, 32 bits wide
  assign xor_1_out = pull_resistor_1_node ^ pull_resistor_2_node;  // XOR_Gate xor_1, 32 bits wide
  assign not_1_out = ~pull_resistor_1_node;  // NOT_Gate not_1, 32 bits wide
  Shifter #(.width(32)) shifter_1 (.in(pull_resistor_1_node), .\dist (bit_extender_1_out), .out(shifter_1_out));
  Shifter #(.shift("lr"), .width(32)) shifter_2 (
    .in(pull_resistor_1_node), .\dist (bit_extender_2_out), .out(shifter_2_out));
  // IntToFP #(.width(32)) inttofp_1: pin names not known; wires that end beside it: pull_resistor_1_node, inttofp_1_p2
  // FPToInt #(.width(32)) fptoint_1: pin names not known; wires that end beside it: pull_resistor_1_node, fptoint_1_p2
  FPAdder fpadder_1 (.a(pull_resistor_1_node), .b(pull_resistor_2_node), .out(fpadder_1_out));
  FPSubtractor fpsubtractor_1 (.a(pull_resistor_1_node), .b(pull_resistor_2_node), .out(fpsubtractor_1_out));
  FPMultiplier fpmultiplier_1 (.a(pull_resistor_1_node), .b(pull_resistor_2_node), .out(fpmultiplier_1_out));
  FPDivider fpdivider_1 (.a(pull_resistor_1_node), .b(pull_resistor_2_node), .out(fpdivider_1_out));
  // FPSquareRoot fpsquareroot_1: pin names not known; wires that end beside it: pull_resistor_1_node, fpsquareroot_1_p2
  // FPTrigonometry fptrigonometry_1: pin names not known; wires that end beside it: pull_resistor_1_node, fptrigonometry_1_p2, fptrigonometry_1_p3, fptrigonometry_1_p4
  Bit_Extender #(.in_width(11), .out_width(5)) bit_extender_3 (.in(func), .out(bit_extender_3_out));
  assign bit_extender_4_out = {{31{adder_1_cout}}, adder_1_cout};  // Bit_Extender bit_extender_4
  assign bit_extender_5_out = {{31{subtractor_1_bout}}, subtractor_1_bout};  // Bit_Extender bit_extender_5
  Multiplexer #(.select(5), .width(32)) multiplexer_1 (
    .in0(adder_1_out), .in1(subtractor_1_out), .in2(multiplier_1_out), .in3(divider_1_out), .in4(or_1_out),
    .in5(and_1_out), .in6(xor_1_out), .in7(not_1_out), .in8(shifter_1_out), .in9(shifter_2_out),
    .in10(divider_1_rem), .in11(multiplier_1_cout), .in12(bit_extender_4_out), .in13(bit_extender_5_out),
    .in14(inttofp_1_p2), .in15(fptoint_1_p2), .in16(fpadder_1_out), .in17(fpsubtractor_1_out),
    .in18(fpmultiplier_1_out), .in19(fpdivider_1_out), .in20(fpsquareroot_1_p2), .in21(fptrigonometry_1_p2),
    .in22(fptrigonometry_1_p4), .in23(fptrigonometry_1_p3), .out(out_5), .sel(bit_extender_3_out));  // open: in24, in25, in26, in27, in28, in29, in30, in31
endmodule

module comp (
  input  [31:0] a,
  input  [31:0] b,
  input  [10:0] func11,
  input  enable,
  input  save_cond,
  output out_6
);

  wire and_1_out, decoder_1_out0, decoder_1_out1, decoder_1_out2, decoder_1_out3, decoder_1_out4,
       decoder_1_out5, decoder_2_out0, decoder_2_out1, decoder_2_out2, decoder_2_out3, decoder_2_out4,
       decoder_2_out5, multiplexer_1_out;
  wire [2:0] comparator_1_gt, pla_1_out, pla_2_out, undriven;
  wire [3:0] bit_extender_1_out;

  PLA #(.in_width(3), .out_width(3), .\table ("010 000 # eq\nx0x 001 # neq\n100 010 # gt\nxx0 011 # gte\n001 100 # lt\n0xx 101 # lte")) pla_1 (
    .in(comparator_1_gt), .out(pla_1_out));
  Comparator #(.width(32)) comparator_1 (
    .a(a), .b(b), .gt(comparator_1_gt[0]), .eq(comparator_1_gt[1]), .lt(comparator_1_gt[2]));
  PLA #(.in_width(3), .out_width(3), .\table ("010 000 # feq\nx0x 001 # fneq\n100 010 # fgt\nxx0 011 # fgte\n001 100 # flt\n0xx 101 # flte")) pla_2 (
    .in(undriven), .out(pla_2_out));
  // FPComparator fpcomparator_1: pin names not known; wires that end beside it: a, b
  Decoder #(.select(3)) decoder_1 (
    .out0(decoder_1_out0), .out1(decoder_1_out1), .out2(decoder_1_out2), .out3(decoder_1_out3),
    .out4(decoder_1_out4), .out5(decoder_1_out5), .sel(pla_1_out), .en(enable));  // open: out6, out7
  Decoder #(.select(3)) decoder_2 (
    .out0(decoder_2_out0), .out1(decoder_2_out1), .out2(decoder_2_out2), .out3(decoder_2_out3),
    .out4(decoder_2_out4), .out5(decoder_2_out5), .sel(pla_2_out), .en(enable));  // open: out6, out7
  Bit_Extender #(.in_width(11), .out_width(4)) bit_extender_1 (.in(func11), .out(bit_extender_1_out));
  Multiplexer #(.select(4)) multiplexer_1 (
    .in0(decoder_1_out0), .in1(decoder_1_out1), .in2(decoder_1_out2), .in3(decoder_1_out3),
    .in4(decoder_1_out4), .in5(decoder_1_out5), .in10(decoder_2_out0), .in11(decoder_2_out1),
    .in12(decoder_2_out2), .in13(decoder_2_out3), .in14(decoder_2_out4), .in15(decoder_2_out5),
    .out(multiplexer_1_out), .sel(bit_extender_1_out));  // open: in6, in7, in8, in9
  and and_1 (and_1_out, enable, save_cond);
  D_Flip_Flop d_ff_1 (.clk(and_1_out), .D(multiplexer_1_out), .Q(out_6));  // open: Qn, preset, reset
endmodule

module decode (
  input  [31:0] in_1,
  output [10:0] func11,
  output [4:0] b,
  output [4:0] a,
  output [4:0] t,
  output alu,
  output comp,
  output mem,
  output load,
  output store,
  output hlt,
  output reg_store,
  output jmp,
  output rel_jmp,
  output [31:0] imm,
  output is_imm,
  output cond,
  output lui
);

  wire not_1_out;
  wire [2:0] pla_1_out;
  wire [6:0] pla_2_out, pull_resistor_1_node;
  wire [10:0] bit_extender_3_out;
  wire [31:0] bit_extender_1_out, bit_extender_2_out, multiplexer_1_out, shifter_1_out;

  PLA #(.in_width(5), .out_width(5), .\table ("11xxx 00101 # uimm_alu\n01111 00110 # lui\nx1xxx 00100 # alu\n10000 01000 # jal\n10001 10000 # jral")) pla_1 (
    .in(in_1[30:26]), .out({rel_jmp, jmp, pla_1_out[2], lui, pla_1_out[0]}));
  PLA #(.in_width(11), .out_width(7), .\table ("000000xxxxx 1000001 # alu\n0000010xxxx 1000010 # comp\n000001100xx 1001100 # load\n000001101xx 0010100 # store\n00001000000 0100000 # hlt")) pla_2 (
    .in(in_1[10:0]), .out(pla_2_out));
  assign bit_extender_1_out = {{16{in_1[15]}}, in_1[15:0]};  // Bit_Extender bit_extender_1
  Multiplexer #(.width(32)) multiplexer_1 (
    .in0(bit_extender_1_out), .in1(bit_extender_2_out), .out(multiplexer_1_out), .sel(pla_1_out[0]));
  assign bit_extender_2_out = {{16{1'b0}}, in_1[15:0]};  // Bit_Extender bit_extender_2
  Shifter #(.width(32)) shifter_1 (.in(bit_extender_2_out), .\dist (5'b01111), .out(shifter_1_out));
  Multiplexer #(.width(11)) multiplexer_2 (.in0(in_1[10:0]), .in1(bit_extender_3_out), .out(func11), .sel(is_imm));
  assign bit_extender_3_out = {{6{1'b0}}, in_1[30:26]};  // Bit_Extender bit_extender_3
  Pull_Resistor pull_resistor_1 (.node({pull_resistor_1_node[6], hlt, store, load, mem, comp, pull_resistor_1_node[0]}));
  assign {pull_resistor_1_node[6], hlt, store, load, mem, comp, pull_resistor_1_node[0]} = not_1_out ? pla_2_out : 7'bz;  // Controlled_Buffer controlled_buffer_1
  not not_1 (not_1_out, is_imm);
  Multiplexer #(.width(32)) multiplexer_3 (.in0(multiplexer_1_out), .in1(shifter_1_out), .out(imm), .sel(lui));
  or or_1 (is_imm, in_1[29], in_1[30]);
  or or_2 (alu, pull_resistor_1_node[0], pla_1_out[2]);
  or or_3 (reg_store, pull_resistor_1_node[6], is_imm);

  assign a = in_1[20:16];
  assign b = in_1[15:11];
  assign cond = in_1[31];
  assign t = in_1[25:21];
endmodule
